// Logisim project CPU.circ as structural Verilog: 8 circuits, main circuit main
module main (
  input  RESET,
  output out_2,
  output out_3,
  output out_4,
  output [15:0] out_5,
  output out_6,
  output out_7,
  output out_8,
  output out_9,
  output [15:0] out_10,
  output [15:0] out_11,
  output out_12,
  output out_13,
  output out_14,
  output out_15,
  output [15:0] out_16,
  output [15:0] out_17,
  output out_18,
  output out_19,
  output out_20,
  output out_21,
  output [7:0] out_22,
  output [15:0] out_23,
  output out_24,
  output out_25,
  output out_26,
  output out_27
);

  wire ALU_A_LOAD_B, ALU_A_LOAD_MBR, ALU_A_LOAD_SP, ALU_ADD, ALU_AND, ALU_B_LOAD_A, ALU_B_LOAD_C,
       ALU_B_LOAD_DATA_BUS, ALU_B_LOAD_MBR, ALU_DIV, ALU_GET_RES, ALU_MUL, ALU_NEG, ALU_OR, ALU_SHL, ALU_SHR,
       ALU_SUB, ALU_XOR, and_1_out, and_2_out, and_3_out, and_4_out, and_5_out, and_6_out, and_7_out,
       and_8_out, and_9_out, B_ADDR_BUS, C_ADDR_BUS, CHECK_NOT_OVERFLOW, CHECK_NOT_POSITIVE, CHECK_NOT_ZERO,
       CHECK_OVERFLOW, CHECK_POSITIVE, CHECK_ZERO, CLK, clock_1_out, d_ff_1_q, DIV_CONT, FINISHED, GET_HIGH,
       HALT, LOAD_MAR, MBR_DATA_BUS, MICRO_CODE_COUNTER, MUL_CONT, not_1_out, not_2_out, not_3_out,
       not_4_out, not_5_out, not_6_out, not_7_out, ONE_TO_ALU, or_1_out, or_2_out, PC_INC, PC_TO_DATA,
       SP_1_TO_MAR, SP_DEC, SP_INC, WAIT, ZERO_CONST, ZERO_FLAG;
  wire [3:0] n8_bitna_displej_logika_1_out_2, n8_bitna_displej_logika_1_out_3,
       n8_bitna_displej_logika_1_out_4, n8_bitna_displej_logika_1_out_5, n8_bitna_displej_logika_2_out_2,
       n8_bitna_displej_logika_2_out_3, n8_bitna_displej_logika_2_out_4, n8_bitna_displej_logika_2_out_5,
       n8_bitna_displej_logika_3_out_2, n8_bitna_displej_logika_3_out_3, n8_bitna_displej_logika_3_out_4,
       n8_bitna_displej_logika_3_out_5, n8_bitna_displej_logika_4_out_2, n8_bitna_displej_logika_4_out_3,
       n8_bitna_displej_logika_4_out_4, n8_bitna_displej_logika_4_out_5, n8_bitna_displej_logika_5_out_2,
       n8_bitna_displej_logika_5_out_3, n8_bitna_displej_logika_5_out_4, n8_bitna_displej_logika_5_out_5,
       n8_bitna_displej_logika_6_out_2, n8_bitna_displej_logika_6_out_3, n8_bitna_displej_logika_6_out_4,
       n8_bitna_displej_logika_6_out_5, n8_bitna_displej_logika_7_out_2, n8_bitna_displej_logika_7_out_3,
       n8_bitna_displej_logika_7_out_4, n8_bitna_displej_logika_7_out_5, n8_bitna_displej_logika_8_out_2,
       n8_bitna_displej_logika_8_out_3, n8_bitna_displej_logika_8_out_4, n8_bitna_displej_logika_8_out_5,
       n8_bitna_displej_logika_9_out_2, n8_bitna_displej_logika_9_out_3, n8_bitna_displej_logika_9_out_4,
       n8_bitna_displej_logika_9_out_5, n8_bitna_displej_logika_10_out_2, n8_bitna_displej_logika_10_out_3,
       n8_bitna_displej_logika_10_out_4, n8_bitna_displej_logika_10_out_5, n8_bitna_displej_logika_11_out_2,
       n8_bitna_displej_logika_11_out_3, n8_bitna_displej_logika_11_out_4, n8_bitna_displej_logika_11_out_5,
       n8_bitna_displej_logika_12_out_2, n8_bitna_displej_logika_12_out_3, n8_bitna_displej_logika_12_out_4,
       n8_bitna_displej_logika_12_out_5, n8_bitna_displej_logika_13_out_2, n8_bitna_displej_logika_13_out_3,
       n8_bitna_displej_logika_13_out_4, n8_bitna_displej_logika_13_out_5, n8_bitna_displej_logika_14_out_2,
       n8_bitna_displej_logika_14_out_3, n8_bitna_displej_logika_14_out_4, n8_bitna_displej_logika_14_out_5,
       n8_bitna_displej_logika_15_out_2, n8_bitna_displej_logika_15_out_3, n8_bitna_displej_logika_15_out_4,
       n8_bitna_displej_logika_15_out_5, n9_bitna_displej_logika_1_out_2, n9_bitna_displej_logika_1_out_3,
       n9_bitna_displej_logika_1_out_4;
  wire [5:0] rom_2_data;
  wire [8:0] MICROCODE_ADDR, multiplexer_2_out;
  wire [8:1] IR_OUT;
  wire [15:0] adder_1_out, adder_2_out, ADDR_BUS, controlled_buffer_1_out, controlled_buffer_2_out,
       controlled_buffer_3_out, DATA_BUS, HIGH_BYTE, multiplexer_1_out, multiplexer_3_out, multiplexer_4_out,
       multiplexer_5_out, multiplexer_6_out, n16_bitni_registar_1_out_7, n16_bitni_registar_3_out_7,
       n16_bitni_registar_4_out_7, n16_bitni_registar_5_out_7, PC, ram_1_data, SP_1;
  wire [31:0] videomemorija_1_p0, videomemorija_1_p1, videomemorija_1_p2, videomemorija_1_p3,
       videomemorija_1_p4, videomemorija_1_p5, videomemorija_1_p6, videomemorija_1_p7, videomemorija_2_p0,
       videomemorija_2_p1, videomemorija_2_p2, videomemorija_2_p3, videomemorija_2_p4, videomemorija_2_p5,
       videomemorija_2_p6, videomemorija_2_p7, videomemorija_3_p0, videomemorija_3_p1, videomemorija_3_p2,
       videomemorija_3_p3, videomemorija_3_p4, videomemorija_3_p5, videomemorija_3_p6, videomemorija_3_p7,
       videomemorija_4_p0, videomemorija_4_p1, videomemorija_4_p2, videomemorija_4_p3, videomemorija_4_p4,
       videomemorija_4_p5, videomemorija_4_p6, videomemorija_4_p7;

  Multiplexer #(.width(16)) multiplexer_1 (
    .in0(controlled_buffer_3_out), .in1(HIGH_BYTE), .out(multiplexer_1_out), .sel(GET_HIGH));  // open: en
  VideoMemorija videomemorija_1 (
    .data_bus(DATA_BUS), .select_mask(2'b00), .address_bus(ADDR_BUS), .MEM_WR(out_9), .RESET(RESET),
    .P7(videomemorija_1_p7), .P6(videomemorija_1_p6), .P5(videomemorija_1_p5), .P1(videomemorija_1_p1),
    .P0(videomemorija_1_p0), .P2(videomemorija_1_p2), .P3(videomemorija_1_p3), .P4(videomemorija_1_p4));
  DotMatrix #(.inputtype("row"), .matrixcols(32), .matrixrows(8)) dotmatrix_1 (
    .row0(videomemorija_1_p0), .row1(videomemorija_1_p1), .row2(videomemorija_1_p2),
    .row3(videomemorija_1_p3), .row4(videomemorija_1_p4), .row5(videomemorija_1_p5),
    .row6(videomemorija_1_p6), .row7(videomemorija_1_p7));
  VideoMemorija videomemorija_2 (
    .data_bus(DATA_BUS), .select_mask(2'b10), .address_bus(ADDR_BUS), .MEM_WR(out_9), .RESET(RESET),
    .P7(videomemorija_2_p7), .P6(videomemorija_2_p6), .P5(videomemorija_2_p5), .P1(videomemorija_2_p1),
    .P0(videomemorija_2_p0), .P2(videomemorija_2_p2), .P3(videomemorija_2_p3), .P4(videomemorija_2_p4));
  DotMatrix #(.inputtype("row"), .matrixcols(32), .matrixrows(8)) dotmatrix_2 (
    .row0(videomemorija_2_p0), .row1(videomemorija_2_p1), .row2(videomemorija_2_p2),
    .row3(videomemorija_2_p3), .row4(videomemorija_2_p4), .row5(videomemorija_2_p5),
    .row6(videomemorija_2_p6), .row7(videomemorija_2_p7));
  Multiplexer #(.select(2), .width(9)) multiplexer_2 (
    .in0({IR_OUT, 1'b0}), .in1(9'h101), .in2(9'h115), .out(multiplexer_2_out), .sel({DIV_CONT, MUL_CONT}));  // open: in3, en
  assign controlled_buffer_1_out = out_18 ? n16_bitni_registar_3_out_7 : 16'bz;  // Controlled_Buffer controlled_buffer_1
  assign controlled_buffer_2_out = out_24 ? n16_bitni_registar_1_out_7 : 16'bz;  // Controlled_Buffer controlled_buffer_2
  _16_bitni_registar u_16_bitni_registar_1 (
    .in_2(controlled_buffer_2_out), .in_1(RESET), .Load(out_24), .Clock(CLK), .Preview(out_23),
    .out_7(n16_bitni_registar_1_out_7), .OE(out_26));
  or or_1 (or_1_out, FINISHED, not_1_out);
  not not_1 (not_1_out, WAIT);
  not not_2 (not_2_out, ZERO_FLAG);
  not not_3 (not_3_out, out_2);
  assign controlled_buffer_3_out = out_12 ? DATA_BUS : 16'bz;  // Controlled_Buffer controlled_buffer_3
  _16_bitni_registar u_16_bitni_registar_2 (
    .in_2(multiplexer_1_out), .in_1(RESET), .Load(out_12), .Clock(CLK), .Preview(out_10), .out_7(DATA_BUS),
    .OE(out_13));
  _16_bitni_registar u_16_bitni_registar_3 (
    .in_2(controlled_buffer_1_out), .in_1(RESET), .Load(out_18), .Clock(CLK), .Preview(out_16),
    .out_7(n16_bitni_registar_3_out_7), .OE(out_19));
  Pull_Resistor #(.pull(1)) pull_resistor_1 (.node(MICRO_CODE_COUNTER));
  and and_1 (and_1_out, CLK, or_1_out);
  or or_2 (or_2_out, RESET, and_2_out, and_3_out, and_4_out, and_5_out, and_7_out, and_6_out, ZERO_CONST);
  and and_2 (and_2_out, CHECK_ZERO, ZERO_FLAG);
  and and_3 (and_3_out, CHECK_NOT_ZERO, not_2_out);
  and and_4 (and_4_out, CHECK_POSITIVE, out_2);
  and and_5 (and_5_out, CHECK_NOT_POSITIVE, not_3_out);
  Demultiplexer #(.width(16), .tristate("true")) demultiplexer_1 (
    .out0(DATA_BUS), .out1(ADDR_BUS), .in(n16_bitni_registar_1_out_7), .sel(C_ADDR_BUS));  // open: en
  ROM #(.addrWidth(9), .dataWidth(32)) rom_1 (
    .addr(MICROCODE_ADDR),
    .data({SP_1_TO_MAR, out_12, out_18, MICRO_CODE_COUNTER, out_19, out_13, out_9, out_6, ALU_NEG, ALU_OR, ALU_AND, ALU_SUB, ALU_ADD, ALU_GET_RES, ALU_A_LOAD_B, ONE_TO_ALU, LOAD_MAR, SP_DEC, out_25, out_27, out_7, out_20, out_8, out_21, out_15, out_14, PC_INC, HALT, SP_INC, out_3, CHECK_ZERO, ZERO_CONST}));  // open: sel
  not not_4 (not_4_out, MICRO_CODE_COUNTER);
  Counter #(.width(9), .max('h1ff)) counter_1 (
    .load(MICRO_CODE_COUNTER), .D(multiplexer_2_out), .count(not_4_out), .Q(MICROCODE_ADDR), .clk(and_1_out),
    .clr(or_2_out));  // open: carry
  and and_6 (and_6_out, CHECK_OVERFLOW, out_4);
  and and_7 (and_7_out, CHECK_NOT_OVERFLOW, not_5_out);
  Demultiplexer #(.width(16)) demultiplexer_2 (
    .out1(controlled_buffer_1_out), .in(DATA_BUS), .sel(out_18));  // open: out0, en
  Demultiplexer #(.width(16), .tristate("true")) demultiplexer_3 (
    .out0(DATA_BUS), .out1(ADDR_BUS), .in(n16_bitni_registar_3_out_7), .sel(B_ADDR_BUS));  // open: en
  Demultiplexer #(.width(16)) demultiplexer_4 (
    .out1(controlled_buffer_2_out), .in(DATA_BUS), .sel(out_24));  // open: out0, en
  Hex_Digit_Display hex_digit_display_1 (.value(n8_bitna_displej_logika_1_out_4));  // open: dp
  Hex_Digit_Display hex_digit_display_2 (.value(n8_bitna_displej_logika_1_out_5));  // open: dp
  Hex_Digit_Display hex_digit_display_3 (.value(n8_bitna_displej_logika_1_out_2));  // open: dp
  _8_bitna_displej_logika u_8_bitna_displej_logika_1 (
    .ULAZ(out_10), .out_2(n8_bitna_displej_logika_1_out_2), .out_3(n8_bitna_displej_logika_1_out_3),
    .out_4(n8_bitna_displej_logika_1_out_4), .out_5(n8_bitna_displej_logika_1_out_5));
  Hex_Digit_Display hex_digit_display_4 (.value(n8_bitna_displej_logika_2_out_5));  // open: dp
  Hex_Digit_Display hex_digit_display_5 (.value(n8_bitna_displej_logika_2_out_4));  // open: dp
  _8_bitna_displej_logika u_8_bitna_displej_logika_2 (
    .ULAZ(ADDR_BUS), .out_2(n8_bitna_displej_logika_2_out_2), .out_3(n8_bitna_displej_logika_2_out_3),
    .out_4(n8_bitna_displej_logika_2_out_4), .out_5(n8_bitna_displej_logika_2_out_5));
  Hex_Digit_Display hex_digit_display_6 (.value(n9_bitna_displej_logika_1_out_3));  // open: dp
  Hex_Digit_Display hex_digit_display_7 (.value(n9_bitna_displej_logika_1_out_2));  // open: dp
  _9_bitna_displej_logika u_9_bitna_displej_logika_1 (
    .out_2(n9_bitna_displej_logika_1_out_2), .out_3(n9_bitna_displej_logika_1_out_3),
    .out_4(n9_bitna_displej_logika_1_out_4), .in_1(MICROCODE_ADDR));
  not not_5 (not_5_out, out_4);
  Hex_Digit_Display hex_digit_display_8 (.value(n8_bitna_displej_logika_3_out_4));  // open: dp
  Hex_Digit_Display hex_digit_display_9 (.value(n8_bitna_displej_logika_3_out_5));  // open: dp
  _8_bitna_displej_logika u_8_bitna_displej_logika_3 (
    .ULAZ(out_10), .out_2(n8_bitna_displej_logika_3_out_2), .out_3(n8_bitna_displej_logika_3_out_3),
    .out_4(n8_bitna_displej_logika_3_out_4), .out_5(n8_bitna_displej_logika_3_out_5));
  Hex_Digit_Display hex_digit_display_10 (.value(n8_bitna_displej_logika_5_out_4));  // open: dp
  Hex_Digit_Display hex_digit_display_11 (.value(n8_bitna_displej_logika_4_out_5));  // open: dp
  Hex_Digit_Display hex_digit_display_12 (.value(n8_bitna_displej_logika_4_out_4));  // open: dp
  _8_bitna_displej_logika u_8_bitna_displej_logika_4 (
    .ULAZ(out_23), .out_2(n8_bitna_displej_logika_4_out_2), .out_3(n8_bitna_displej_logika_4_out_3),
    .out_4(n8_bitna_displej_logika_4_out_4), .out_5(n8_bitna_displej_logika_4_out_5));
  VideoMemorija videomemorija_3 (
    .data_bus(DATA_BUS), .select_mask(2'b01), .address_bus(ADDR_BUS), .MEM_WR(out_9), .RESET(RESET),
    .P7(videomemorija_3_p7), .P6(videomemorija_3_p6), .P5(videomemorija_3_p5), .P1(videomemorija_3_p1),
    .P0(videomemorija_3_p0), .P2(videomemorija_3_p2), .P3(videomemorija_3_p3), .P4(videomemorija_3_p4));
  VideoMemorija videomemorija_4 (
    .data_bus(DATA_BUS), .select_mask(2'b11), .address_bus(ADDR_BUS), .MEM_WR(out_9), .RESET(RESET),
    .P7(videomemorija_4_p7), .P6(videomemorija_4_p6), .P5(videomemorija_4_p5), .P1(videomemorija_4_p1),
    .P0(videomemorija_4_p0), .P2(videomemorija_4_p2), .P3(videomemorija_4_p3), .P4(videomemorija_4_p4));
  Hex_Digit_Display hex_digit_display_13 (.value(n8_bitna_displej_logika_1_out_3));  // open: dp
  Hex_Digit_Display hex_digit_display_14 (.value(n8_bitna_displej_logika_2_out_3));  // open: dp
  Hex_Digit_Display hex_digit_display_15 (.value(n8_bitna_displej_logika_2_out_2));  // open: dp
  Hex_Digit_Display hex_digit_display_16 (.value(n9_bitna_displej_logika_1_out_4));  // open: dp
  Hex_Digit_Display hex_digit_display_17 (.value(n8_bitna_displej_logika_3_out_2));  // open: dp
  Hex_Digit_Display hex_digit_display_18 (.value(n8_bitna_displej_logika_3_out_3));  // open: dp
  Hex_Digit_Display hex_digit_display_19 (.value(n8_bitna_displej_logika_5_out_5));  // open: dp
  Hex_Digit_Display hex_digit_display_20 (.value(n8_bitna_displej_logika_5_out_2));  // open: dp
  _8_bitna_displej_logika u_8_bitna_displej_logika_5 (
    .ULAZ(out_16), .out_2(n8_bitna_displej_logika_5_out_2), .out_3(n8_bitna_displej_logika_5_out_3),
    .out_4(n8_bitna_displej_logika_5_out_4), .out_5(n8_bitna_displej_logika_5_out_5));
  Hex_Digit_Display hex_digit_display_21 (.value(n8_bitna_displej_logika_4_out_3));  // open: dp
  Hex_Digit_Display hex_digit_display_22 (.value(n8_bitna_displej_logika_4_out_2));  // open: dp
  DotMatrix #(.inputtype("row"), .matrixcols(32), .matrixrows(8)) dotmatrix_3 (
    .row0(videomemorija_3_p0), .row1(videomemorija_3_p1), .row2(videomemorija_3_p2),
    .row3(videomemorija_3_p3), .row4(videomemorija_3_p4), .row5(videomemorija_3_p5),
    .row6(videomemorija_3_p6), .row7(videomemorija_3_p7));
  DotMatrix #(.inputtype("row"), .matrixcols(32), .matrixrows(8)) dotmatrix_4 (
    .row0(videomemorija_4_p0), .row1(videomemorija_4_p1), .row2(videomemorija_4_p2),
    .row3(videomemorija_4_p3), .row4(videomemorija_4_p4), .row5(videomemorija_4_p5),
    .row6(videomemorija_4_p6), .row7(videomemorija_4_p7));
  Hex_Digit_Display hex_digit_display_23 (.value(n8_bitna_displej_logika_6_out_4));  // open: dp
  Hex_Digit_Display hex_digit_display_24 (.value(n8_bitna_displej_logika_7_out_4));  // open: dp
  Hex_Digit_Display hex_digit_display_25 (.value(n8_bitna_displej_logika_5_out_3));  // open: dp
  Hex_Digit_Display hex_digit_display_26 (.value(n8_bitna_displej_logika_6_out_2));  // open: dp
  Hex_Digit_Display hex_digit_display_27 (.value(n8_bitna_displej_logika_6_out_5));  // open: dp
  _8_bitna_displej_logika u_8_bitna_displej_logika_6 (
    .ULAZ(out_16), .out_2(n8_bitna_displej_logika_6_out_2), .out_3(n8_bitna_displej_logika_6_out_3),
    .out_4(n8_bitna_displej_logika_6_out_4), .out_5(n8_bitna_displej_logika_6_out_5));
  Hex_Digit_Display hex_digit_display_28 (.value(n8_bitna_displej_logika_7_out_5));  // open: dp
  Hex_Digit_Display hex_digit_display_29 (.value(n8_bitna_displej_logika_7_out_2));  // open: dp
  _8_bitna_displej_logika u_8_bitna_displej_logika_7 (
    .ULAZ(DATA_BUS), .out_2(n8_bitna_displej_logika_7_out_2), .out_3(n8_bitna_displej_logika_7_out_3),
    .out_4(n8_bitna_displej_logika_7_out_4), .out_5(n8_bitna_displej_logika_7_out_5));
  Hex_Digit_Display hex_digit_display_30 (.value(n8_bitna_displej_logika_6_out_3));  // open: dp
  Hex_Digit_Display hex_digit_display_31 (.value(n8_bitna_displej_logika_7_out_3));  // open: dp
  Hex_Digit_Display hex_digit_display_32 (.value(n8_bitna_displej_logika_8_out_5));  // open: dp
  Hex_Digit_Display hex_digit_display_33 (.value(n8_bitna_displej_logika_8_out_4));  // open: dp
  Hex_Digit_Display hex_digit_display_34 (.value(n8_bitna_displej_logika_9_out_5));  // open: dp
  Hex_Digit_Display hex_digit_display_35 (.value(n8_bitna_displej_logika_9_out_4));  // open: dp
  Hex_Digit_Display hex_digit_display_36 (.value(n8_bitna_displej_logika_8_out_3));  // open: dp
  Hex_Digit_Display hex_digit_display_37 (.value(n8_bitna_displej_logika_8_out_2));  // open: dp
  _8_bitna_displej_logika u_8_bitna_displej_logika_8 (
    .ULAZ(out_23), .out_2(n8_bitna_displej_logika_8_out_2), .out_3(n8_bitna_displej_logika_8_out_3),
    .out_4(n8_bitna_displej_logika_8_out_4), .out_5(n8_bitna_displej_logika_8_out_5));
  Hex_Digit_Display hex_digit_display_38 (.value(n8_bitna_displej_logika_9_out_3));  // open: dp
  Hex_Digit_Display hex_digit_display_39 (.value(n8_bitna_displej_logika_9_out_2));  // open: dp
  _8_bitna_displej_logika u_8_bitna_displej_logika_9 (
    .ULAZ(out_5), .out_2(n8_bitna_displej_logika_9_out_2), .out_3(n8_bitna_displej_logika_9_out_3),
    .out_4(n8_bitna_displej_logika_9_out_4), .out_5(n8_bitna_displej_logika_9_out_5));
  Multiplexer #(.select(2), .width(16)) multiplexer_3 (
    .in0(DATA_BUS), .in1(adder_1_out), .in2(SP_1), .out(multiplexer_3_out), .sel({SP_DEC, SP_INC}));  // open: in3, en
  _8_bitni_registar IR (
    .OE(out_25), .Load(out_27), .Clock(CLK), .in_2(DATA_BUS[7:0]), .out_7({IR_OUT[7:1], IR_OUT[8]}),
    .RESET(RESET), .Preview(out_22));
  Clock clock_1 (.out(clock_1_out));
  Hex_Digit_Display hex_digit_display_40 (.value(n8_bitna_displej_logika_11_out_4));  // open: dp
  assign DATA_BUS = out_6 ? ram_1_data : 16'bz;  // Controlled_Buffer controlled_buffer_4
  RAM #(.addrWidth(16), .dataWidth(16), .bus("separate")) ram_1 (
    .addr(ADDR_BUS), .din(DATA_BUS), .data(ram_1_data), .str(out_9), .clk(CLK), .ld(out_6));  // open: sel, clr
  _16_bitni_registar u_16_bitni_registar_4 (
    .in_2(DATA_BUS), .in_1(RESET), .Load(out_21), .Clock(CLK), .Preview(out_17),
    .out_7(n16_bitni_registar_4_out_7), .OE(out_20));
  D_Flip_Flop d_ff_1 (.Q(d_ff_1_q), .preset(RESET), .reset(HALT));  // open: clk, D, Qn, en
  assign CLK = d_ff_1_q ? clock_1_out : 1'bz;  // Controlled_Buffer controlled_buffer_5
  Hex_Digit_Display hex_digit_display_41 (.value(n8_bitna_displej_logika_10_out_4));  // open: dp
  Hex_Digit_Display hex_digit_display_42 (.value(n8_bitna_displej_logika_10_out_5));  // open: dp
  _8_bitna_displej_logika u_8_bitna_displej_logika_10 (
    .ULAZ(HIGH_BYTE), .out_2(n8_bitna_displej_logika_10_out_2), .out_3(n8_bitna_displej_logika_10_out_3),
    .out_4(n8_bitna_displej_logika_10_out_4), .out_5(n8_bitna_displej_logika_10_out_5));
  Hex_Digit_Display hex_digit_display_43 (.value(n8_bitna_displej_logika_11_out_5));  // open: dp
  Hex_Digit_Display hex_digit_display_44 (.value(n8_bitna_displej_logika_11_out_2));  // open: dp
  _8_bitna_displej_logika u_8_bitna_displej_logika_11 (
    .ULAZ(out_11), .out_2(n8_bitna_displej_logika_11_out_2), .out_3(n8_bitna_displej_logika_11_out_3),
    .out_4(n8_bitna_displej_logika_11_out_4), .out_5(n8_bitna_displej_logika_11_out_5));
  _16_bitni_registar u_16_bitni_registar_5 (
    .in_2(multiplexer_3_out), .in_1(RESET), .Load(out_15), .Clock(CLK), .Preview(out_11),
    .out_7(n16_bitni_registar_5_out_7), .OE(out_14));
  Hex_Digit_Display hex_digit_display_45 (.value(n8_bitna_displej_logika_10_out_3));  // open: dp
  Hex_Digit_Display hex_digit_display_46 (.value(n8_bitna_displej_logika_10_out_2));  // open: dp
  Hex_Digit_Display hex_digit_display_47 (.value(n8_bitna_displej_logika_11_out_3));  // open: dp
  Demultiplexer #(.width(16), .tristate("true")) demultiplexer_5 (
    .out0(DATA_BUS), .out1(ADDR_BUS), .in(n16_bitni_registar_4_out_7), .sel(and_8_out), .en(out_20));
  Hex_Digit_Display hex_digit_display_48 (.value(n8_bitna_displej_logika_12_out_4));  // open: dp
  Multiplexer #(.width(16)) multiplexer_4 (
    .in0(DATA_BUS), .in1(adder_2_out), .out(multiplexer_4_out), .sel(PC_INC));  // open: en
  Adder #(.width(16)) adder_1 (.a(out_11), .b(16'h1), .out(adder_1_out));  // open: cin, cout
  Demultiplexer #(.width(16), .tristate("true")) demultiplexer_6 (
    .out0(DATA_BUS), .out1(ADDR_BUS), .in(n16_bitni_registar_5_out_7), .sel(LOAD_MAR), .en(out_14));
  and and_8 (and_8_out, LOAD_MAR, not_6_out);
  Hex_Digit_Display hex_digit_display_49 (.value(n8_bitna_displej_logika_12_out_2));  // open: dp
  Hex_Digit_Display hex_digit_display_50 (.value(n8_bitna_displej_logika_12_out_5));  // open: dp
  _8_bitna_displej_logika u_8_bitna_displej_logika_12 (
    .ULAZ(out_17), .out_2(n8_bitna_displej_logika_12_out_2), .out_3(n8_bitna_displej_logika_12_out_3),
    .out_4(n8_bitna_displej_logika_12_out_4), .out_5(n8_bitna_displej_logika_12_out_5));
  not not_6 (not_6_out, MBR_DATA_BUS);
  Hex_Digit_Display hex_digit_display_51 (.value(n8_bitna_displej_logika_12_out_3));  // open: dp
  _16_bitni_registar u_16_bitni_registar_6 (
    .in_2(multiplexer_4_out), .in_1(RESET), .Load(out_8), .Clock(CLK), .Preview(out_5), .out_7(PC), .OE(out_7));
  Subtractor #(.width(16)) subtractor_1 (.a(out_11), .b(16'h1), .out(SP_1));  // open: bin, bout
  assign ADDR_BUS = SP_1_TO_MAR ? SP_1 : 16'bz;  // Controlled_Buffer controlled_buffer_6
  ROM #(.addrWidth(9), .dataWidth(32)) rom_2 (
    .addr(MICROCODE_ADDR),
    .data({ALU_B_LOAD_DATA_BUS, ALU_A_LOAD_SP, MBR_DATA_BUS, ALU_A_LOAD_MBR, ALU_B_LOAD_MBR, CHECK_NOT_ZERO, B_ADDR_BUS, PC_TO_DATA, CHECK_POSITIVE, CHECK_NOT_POSITIVE, CHECK_OVERFLOW, CHECK_NOT_OVERFLOW, ALU_SHR, ALU_SHL, ALU_DIV, ALU_MUL, GET_HIGH, out_24, out_26, C_ADDR_BUS, DIV_CONT, MUL_CONT, ALU_B_LOAD_C, ALU_XOR, WAIT, ALU_B_LOAD_A, rom_2_data}));  // open: sel
  Multiplexer #(.select(3), .width(16)) multiplexer_5 (
    .in0(out_10), .in1(out_16), .in2(out_17), .in3(out_23), .in4(out_11), .out(multiplexer_5_out),
    .sel({ALU_A_LOAD_SP, ALU_A_LOAD_MBR, ALU_A_LOAD_B}));  // open: in5, in6, in7, en
  Adder #(.width(16)) adder_2 (.a(out_5), .b(16'h1), .out(adder_2_out));  // open: cin, cout
  Hex_Digit_Display hex_digit_display_52 (.value(n8_bitna_displej_logika_13_out_5));  // open: dp
  Hex_Digit_Display hex_digit_display_53 (.value(n8_bitna_displej_logika_13_out_4));  // open: dp
  _8_bitna_displej_logika u_8_bitna_displej_logika_13 (
    .ULAZ(out_17), .out_2(n8_bitna_displej_logika_13_out_2), .out_3(n8_bitna_displej_logika_13_out_3),
    .out_4(n8_bitna_displej_logika_13_out_4), .out_5(n8_bitna_displej_logika_13_out_5));
  Demultiplexer #(.width(16), .tristate("true")) demultiplexer_7 (
    .out0(DATA_BUS), .out1(ADDR_BUS), .in(PC), .sel(and_9_out), .en(out_7));
  and and_9 (and_9_out, LOAD_MAR, not_7_out);
  Hex_Digit_Display hex_digit_display_54 (.value(n8_bitna_displej_logika_15_out_4));  // open: dp
  Hex_Digit_Display hex_digit_display_55 (.value(n8_bitna_displej_logika_13_out_3));  // open: dp
  Hex_Digit_Display hex_digit_display_56 (.value(n8_bitna_displej_logika_13_out_2));  // open: dp
  ALU alu_1 (
    .A(multiplexer_5_out), .ADD(ALU_ADD), .SUB(ALU_SUB), .AND(ALU_AND), .OR(ALU_OR), .NEG(ALU_NEG),
    .B(multiplexer_6_out), .RES_2(DATA_BUS), .CLK(CLK), .GET_RES(ALU_GET_RES), .ZERO(ZERO_FLAG),
    .MARK_FLAG(out_3), .OVERFLOW(out_4), .out_20(out_2), .SHL(ALU_SHL), .SHR(ALU_SHR), .MUL(ALU_MUL),
    .High(HIGH_BYTE), .DIV(ALU_DIV), .RES(RESET), .XOR(ALU_XOR), .FINISHED(FINISHED));
  not not_7 (not_7_out, PC_TO_DATA);
  Hex_Digit_Display hex_digit_display_57 (.value(n8_bitna_displej_logika_14_out_5));  // open: dp
  Hex_Digit_Display hex_digit_display_58 (.value(n8_bitna_displej_logika_14_out_4));  // open: dp
  _8_bitna_displej_logika u_8_bitna_displej_logika_14 (
    .ULAZ(out_5), .out_2(n8_bitna_displej_logika_14_out_2), .out_3(n8_bitna_displej_logika_14_out_3),
    .out_4(n8_bitna_displej_logika_14_out_4), .out_5(n8_bitna_displej_logika_14_out_5));
  Hex_Digit_Display hex_digit_display_59 (.value(n8_bitna_displej_logika_15_out_5));  // open: dp
  Hex_Digit_Display hex_digit_display_60 (.value(n8_bitna_displej_logika_15_out_2));  // open: dp
  _8_bitna_displej_logika u_8_bitna_displej_logika_15 (
    .ULAZ(out_11), .out_2(n8_bitna_displej_logika_15_out_2), .out_3(n8_bitna_displej_logika_15_out_3),
    .out_4(n8_bitna_displej_logika_15_out_4), .out_5(n8_bitna_displej_logika_15_out_5));
  Hex_Digit_Display hex_digit_display_61 (.value(n8_bitna_displej_logika_14_out_3));  // open: dp
  Hex_Digit_Display hex_digit_display_62 (.value(n8_bitna_displej_logika_14_out_2));  // open: dp
  Hex_Digit_Display hex_digit_display_63 (.value(n8_bitna_displej_logika_15_out_3));  // open: dp
  Multiplexer #(.select(4), .width(16)) multiplexer_6 (
    .in0(out_16), .in1(16'h1), .in2(out_17), .in4(out_23), .in8(out_10), .out(multiplexer_6_out),
    .sel({ALU_B_LOAD_A, ALU_B_LOAD_C, ALU_B_LOAD_MBR, ONE_TO_ALU}));  // open: in3, in5, in6, in7, in9, in10, in11, in12, in13, in14, in15, en

  // Other names for the same wires on the sheet: MARK_FLAG = out_3; SP_OE = out_14; LOAD_SP = out_15;
  //   LOAD_MBR = out_21; LOAD_PC = out_8; MBR_OE = out_20; PC_OE = out_7; LOAD_IR = out_27; IR_OE = out_25;
  //   MEM_RD = out_6; MEM_WR = out_9; OE_A = out_13; OE_B = out_19; LOAD_B = out_18; LOAD_A = out_12; OE_C = out_26;
  //   LOAD_C = out_24; A[15:0] = out_10; B[15:0] = out_16; C[15:0] = out_23; MBR[15:0] = out_17;
  //   MBR_PREV[15:0] = out_17; OVERFLOW_FLAG = out_4; PC_PREV[15:0] = out_5; POSITIVE_FLAG = out_2; SP[15:0] = out_11;
  //   SP_PREV[15:0] = out_11

  // Notes on the sheet:
  //   Adresa je od 0xFFF0 - 0xFFF3
  //   Adresa je od 0xFFF8 - 0xFFFB
  //   contents of rom_1 (hex, n*v repeats v):
  //   1009800 220 10002000 0 48000000 1 24000000 1 41008a20 1 21008a20 1 49000000 1 1008b20 e0100 41008400
  //   1 1008aa0 1 20000040 1 8000080 1 400c0004 1 40140004 1 1008b20 c0084 1 0 1008b20 140084 1 0 9008100
  //   400c0004 1 0 9008100 40140004 1 0 1008b20 e0100 1008500 400c0000 1 0 1008b20 e0100 1008500 40140000
  //   1 0 1008b20 400c0004 1 0 1008b20 40140004 1 0 140004 1 9008100 140004 1 0 1008b20 140004 1 0
  //   40150004 1 400d0004 1 20170004 1 200f0004 1 9008100 150104 a000400 1 9008100 d0104 a000400 1
  //   40240004 1 40440004 1 9008100 40240004 1 0 9008100 40440004 1 0 1008b20 40240004 1 0 1008b20
  //   40440004 1 0 40840004 1 1008b20 20084c8 1 0 60080c8 1 c100c080 1 a0080c8 1 a100c080 1 100ca00 1
  //   1008b20 0 600 1 1008b20 2 600 1 1008b20 20088c8 600 1 8100c280 1 1008b20 6008400 1 0 1008b20 a008400
  //   1 0 e000000 1 1008b20 e0100 6008400 1 1008b20 0 600 1 1008b20 0 600 1 1008b20 0 600 1 1008b20 0 600
  //   1 1008b20 e0100 1008500 40240000 1 0 1008b20 e0100 1008500 40440000 1 0 40040004 1 40140004 1
  //   9008100 400c0004 1 0 9008100 40140004 1 0 1008b20 e0100 1008500 400c0000 1 0 1008b20 e0100 1008500
  //   40140000 1 0 1008b20 400c0004 1 0 1008b20 40140004 1 0 1008b20 0 20088c8 600 1 0 1008b20 2 20088c8
  //   600 1 0 1008b20 0 20088c8 600 1 0 1008b20 0 20088c8 600 1 0 1008b20 0 20088c8 600 1 0 1008b20 0
  //   20088c8 600 1 0 40000000 1 6*0 40040004 1 18*0 40040004 1 16*0 1008b20 160004 1 0 1008a20 1 6000000
  //   1 1008b20 e0100 6008400 1 150004 1 f0004 1 4000000 1 8000000 1 20080c8 1 8100c080 1 1008b20 e0100
  //   1008500 0 0 10000000 1008b20 e0100 1008500 0 0 10000000 1008b20 0 0 10000000 1008b20 0 0 10000000
  //   40000000 1 20000000 1 41000000 1 1008b20 e0100 41008400 1 0 10000000 0 10000000 40040004 1 40040004
  //   1 1008b20 e0100 1008500 40040000 1 0 9008100 40040004 1 0 1008b20 e0100 1008500 140004 1 0 400c0004
  //   1 40140004 1 1008b20 e0100 c0100 6008400 1 0 1008b20 e0100 1008500 140004 1 121*0 10
  //   Adresa je od 0xFFF4 - 0xFFF7
  //   Adresa je od 0xFFFC - 0xFFFF
  //   RAM memorija
  //   contents of rom_2 (hex, n*v repeats v):
  //   12*0 2000000 0 0 8000000 13*0 48000000 0 0 0 48000000 0 0 2000000 8000000 0 0 2000000 8000000 0 0 0
  //   8000000 0 8000000 0 0 8000000 8000000 0 8000000 0 0 0 8000000 0 0 0 8000000 4*0 2000000 8000000 0 0
  //   0 8000000 10*0 2000000 10000000 2000000 0 2000000 10000000 2000000 5*0 2000000 8000000 0 0 2000000
  //   8000000 0 0 0 8000000 0 0 0 8000000 5*0 20000000 13*0 4000000 7*0 1000000 12*0 2000000 0 0 8000000 0
  //   0 0 400000 0 0 0 800000 0 0 0 100000 0 0 0 200000 0 0 0 8000000 0 8000000 0 0 0 8000000 0 8000000
  //   6*0 2000000 8000000 0 0 2000000 8000000 0 0 0 8000000 0 8000000 0 0 0 8000000 0 8000000 0 0 0
  //   8000000 0 0 0 8000000 0 0 0 4000000 1000000 5*0 1000000 4*0 400000 10000 4*0 800000 10000 4*0 100000
  //   10000 4*0 200000 10000 0 0 0 8000 5*0 10000 80 18*0 20000 80 19*0 8000000 0 0 4000 0 3000 0 0
  //   18000000 0 0 10004000 0 10004000 0 4000 0 4000 0 2000 0 4000 0 0 8000000 0 8010000 8000000 400 0
  //   8000000 0 8020000 8000000 800 0 8010000 8000000 400 0 8020000 8000000 800 2000 0 2000 0 3000 0 0
  //   18000000 0 0 10200 600 20200 a00 100 0 300 0 0 8000000 0 8000100 0 0 2000000 8000100 0 0 0 8000000 0
  //   8000000 0 0 200 0 200 0 0 8000000 10000200 4*0 8000000 0 10000040
endmodule

module _16_bitni_registar (
  input  in_1,
  input  [15:0] in_2,
  input  OE,
  input  Load,
  input  Clock,
  output [15:0] Preview,
  output [15:0] out_7
);

  Register #(.width(16)) register_1 (.D(in_2), .en(Load), .Q(Preview), .clk(Clock), .clr(in_1));
  assign out_7 = OE ? Preview : 16'bz;  // Controlled_Buffer controlled_buffer_1
endmodule

module _8_bitni_registar (
  input  RESET,
  input  [7:0] in_2,
  input  OE,
  input  Load,
  input  Clock,
  output [7:0] Preview,
  output [7:0] out_7
);

  _4_bit_registar u_4_bit_registar_1 (
    .D3(in_2[7]), .D2(in_2[6]), .D1(in_2[5]), .D0(in_2[4]), .Load(Load), .Clock(Clock), .O3(out_7[7]),
    .O2(out_7[6]), .O1(out_7[5]), .O0(out_7[4]), .Output_Enable(OE), .Clear(RESET), .Preview(Preview[7:4]));  // open: Preset
  _4_bit_registar u_4_bit_registar_2 (
    .D3(in_2[3]), .D2(in_2[2]), .D1(in_2[1]), .D0(in_2[0]), .Load(Load), .Clock(Clock), .O3(out_7[3]),
    .O2(out_7[2]), .O1(out_7[1]), .O0(out_7[0]), .Output_Enable(OE), .Clear(RESET), .Preview(Preview[3:0]));  // open: Preset
endmodule

module _4_bit_registar (
  input  D3,
  input  D2,
  input  D1,
  input  D0,
  input  Output_Enable,
  input  Load,
  input  Clock,
  input  Preset,
  input  Clear,
  output O3,
  output O2,
  output O1,
  output O0,
  output [3:0] Preview
);

  wire and_1_out, and_2_out, and_3_out, and_4_out, and_5_out, and_6_out, and_7_out, and_8_out, not_1_out,
       or_1_out, or_2_out, or_3_out, or_4_out;

  not not_1 (not_1_out, Load);
  and and_1 (and_1_out, Preview[3], not_1_out);
  and and_2 (and_2_out, Load, D3);
  and and_3 (and_3_out, Preview[2], not_1_out);
  and and_4 (and_4_out, Load, D2);
  and and_5 (and_5_out, Preview[1], not_1_out);
  and and_6 (and_6_out, Load, D1);
  and and_7 (and_7_out, Preview[0], not_1_out);
  and and_8 (and_8_out, Load, D0);
  or or_1 (or_1_out, and_1_out, and_2_out);
  or or_2 (or_2_out, and_3_out, and_4_out);
  or or_3 (or_3_out, and_5_out, and_6_out);
  or or_4 (or_4_out, and_7_out, and_8_out);
  D_Flip_Flop d_ff_1 (
    .clk(Clock), .D(or_1_out), .Q(Preview[3]), .preset(Preset), .en(1'b1), .reset(Clear));  // open: Qn
  D_Flip_Flop d_ff_2 (
    .clk(Clock), .D(or_2_out), .Q(Preview[2]), .preset(Preset), .en(1'b1), .reset(Clear));  // open: Qn
  D_Flip_Flop d_ff_3 (
    .clk(Clock), .D(or_3_out), .Q(Preview[1]), .preset(Preset), .en(1'b1), .reset(Clear));  // open: Qn
  D_Flip_Flop d_ff_4 (
    .clk(Clock), .D(or_4_out), .Q(Preview[0]), .preset(Preset), .en(1'b1), .reset(Clear));  // open: Qn
  assign O3 = Output_Enable ? Preview[3] : 1'bz;  // Controlled_Buffer controlled_buffer_1
  assign O2 = Output_Enable ? Preview[2] : 1'bz;  // Controlled_Buffer controlled_buffer_2
  assign O1 = Output_Enable ? Preview[1] : 1'bz;  // Controlled_Buffer controlled_buffer_3
  assign O0 = Output_Enable ? Preview[0] : 1'bz;  // Controlled_Buffer controlled_buffer_4
endmodule

module ALU (
  input  RES,
  input  [15:0] B,
  input  GET_RES,
  input  [15:0] A,
  input  ADD,
  input  SUB,
  input  AND,
  input  MARK_FLAG,
  input  OR,
  input  NEG,
  input  CLK,
  input  SHL,
  input  SHR,
  input  XOR,
  input  MUL,
  input  DIV,
  output [15:0] RES_2,
  output OVERFLOW,
  output FINISHED,
  output out_20,
  output ZERO,
  output [15:0] High
);

  wire A7, A_M, A_M_t, A_out, A_POSITIVE, and_5_out, and_6_out, and_7_out, ARESET, clock_1_out, clock_2_out,
       d_ff_4_q, d_ff_5_q, d_ff_8_q, D_LOAD_INTO_A, D_LOAD_INTO_M, D_LOAD_INTO_Q, D_SHIFT, DCLK, DO_DIV,
       DREPEAT, DSTOP, KOMPLEMENT_OSTATKA, KOMPLEMENT_REZULTATA, LOAD_INTO_A, LOAD_INTO_M, LOAD_INTO_Q,
       LOAD_OR_NOT, MCLK, MRESET, MUL_DIV_OFF, multiplexer_3_out, multiplexer_4_out, multiplexer_5_out,
       NMRESET, nor_1_out, nor_2_out, not_1_out, not_3_out, not_4_out, not_5_out, not_7_out, not_8_out,
       not_9_out, not_10_out, not_11_out, not_12_out, not_13_out, not_14_out, not_15_out, not_16_out,
       not_17_out, not_18_out, not_19_out, NOT_MUL_OR_DIV, or_2_out, or_6_out, or_7_out, or_8_out,
       pull_resistor_3_node, pull_resistor_4_node, Q0, Q_1_q, Q_out, Q_q0, REPEAT, SHIFT, STOP, xor_2_out,
       xor_3_out;
  wire [5:1] counter_3_q, counter_4_q;
  wire [7:0] counter_1_q, counter_2_q;
  wire [7:4] rom_1_data, rom_2_data;
  wire [14:0] AMul;
  wire [15:0] Abs_Ain, Abs_Bin, adder_1_out, adder_2_out, ADivIn, and_1_out, controlled_buffer_2_out,
       controlled_buffer_9_out, DIV_REM, DIV_RES, M, MDiv, multiplexer_6_out, multiplexer_9_out,
       negator_1_out, negator_2_out, negator_3_out, negator_4_out, negator_5_out, or_3_out, Ostatak, QDiv,
       RESULT, shifter_1_out, shifter_2_out, subtractor_2_out, subtractor_3_out, To_Ain, xor_1_out;
  wire [15:1] QMul;

  Clock clock_1 (.out(clock_1_out));
  Pull_Resistor #(.pull(1)) pull_resistor_1 (.node(REPEAT));
  not not_1 (not_1_out, REPEAT);
  not not_2 (A_POSITIVE, ADivIn[15]);
  Pull_Resistor #(.pull(1)) pull_resistor_2 (.node(DREPEAT));
  Pull_Resistor #(.pull(1)) pull_resistor_3 (.node(pull_resistor_3_node));
  not not_3 (not_3_out, pull_resistor_3_node);
  Counter counter_1 (
    .load(not_1_out), .D(8'h1), .count(REPEAT), .Q(counter_1_q), .clk(MCLK), .clr(MUL));  // open: carry
  or or_1 (MRESET, MUL, DIV);
  nor nor_1 (nor_1_out, MUL, DIV);
  D_Flip_Flop d_ff_1 (.clk(MRESET), .D(DIV), .Q(DO_DIV), .reset(NOT_MUL_OR_DIV));  // open: Qn, preset, en
  Subtractor #(.width(16)) subtractor_1 (.a(Ostatak), .b(MDiv), .out(ADivIn));  // open: bin, bout
  assign DCLK = not_4_out ? clock_1_out : 1'bz;  // Controlled_Buffer controlled_buffer_1
  not not_4 (not_4_out, DSTOP);
  not not_5 (not_5_out, DREPEAT);
  Counter counter_2 (
    .load(not_5_out), .D(8'h1), .count(DREPEAT), .Q(counter_2_q), .clk(DCLK), .clr(DIV));  // open: carry
  not not_6 (NMRESET, MRESET);
  Counter #(.width(6), .max('h3f)) counter_3 (
    .load(not_3_out), .count(pull_resistor_3_node), .Q({counter_3_q, DREPEAT}), .clk(DCLK), .clr(MRESET));  // open: D, carry
  Negator #(.width(16)) negator_1 (.in(QDiv), .out(negator_1_out));
  Negator #(.width(16)) negator_2 (.in(Ostatak), .out(negator_2_out));
  or or_2 (or_2_out, A_M, LOAD_INTO_A, A_M_t);
  D_Flip_Flop d_ff_2 (.clk(MCLK), .D(nor_1_out), .Q(MUL_DIV_OFF), .reset(NOT_MUL_OR_DIV));  // open: Qn, preset, en
  Multiplexer #(.width(16)) multiplexer_1 (
    .in0(QDiv), .in1(negator_1_out), .out(DIV_RES), .sel(KOMPLEMENT_REZULTATA));  // open: en
  Multiplexer #(.width(16)) multiplexer_2 (
    .in0(Ostatak), .in1(negator_2_out), .out(DIV_REM), .sel(KOMPLEMENT_OSTATKA));  // open: en
  Adder #(.width(16)) adder_1 (.a(A), .b(B), .out(adder_1_out));  // open: cin, cout
  Subtractor #(.width(16)) subtractor_2 (.a(A), .b(B), .out(subtractor_2_out));  // open: bin, bout
  assign and_1_out = A & B;  // AND_Gate and_1, 16 bits wide
  assign or_3_out = A | B;  // OR_Gate or_3, 16 bits wide
  Negator #(.width(16)) negator_3 (.in(A), .out(negator_3_out));
  Shifter #(.width(16)) shifter_1 (.in(A), .\dist (B[3:0]), .out(shifter_1_out));
  Shifter #(.width(16), .shift("ar")) shifter_2 (.in(A), .\dist (B[3:0]), .out(shifter_2_out));
  or or_4 (NOT_MUL_OR_DIV, OR, SHR, SHL, NEG, AND, SUB, ADD, XOR);
  Multiplexer multiplexer_3 (.in0(or_2_out), .in1(1'b0), .out(multiplexer_3_out), .sel(SHIFT));  // open: en
  ROM rom_1 (.addr(counter_1_q), .data({rom_1_data, SHIFT, LOAD_INTO_A, LOAD_INTO_Q, LOAD_INTO_M}));  // open: sel
  and and_2 (DSTOP, DREPEAT, counter_3_q[5]);
  assign controlled_buffer_2_out = ADD ? adder_1_out : 16'bz;  // Controlled_Buffer controlled_buffer_2
  assign controlled_buffer_2_out = SUB ? subtractor_2_out : 16'bz;  // Controlled_Buffer controlled_buffer_3
  assign controlled_buffer_2_out = AND ? and_1_out : 16'bz;  // Controlled_Buffer controlled_buffer_4
  assign controlled_buffer_2_out = OR ? or_3_out : 16'bz;  // Controlled_Buffer controlled_buffer_5
  assign controlled_buffer_2_out = NEG ? negator_3_out : 16'bz;  // Controlled_Buffer controlled_buffer_6
  assign controlled_buffer_2_out = SHL ? shifter_1_out : 16'bz;  // Controlled_Buffer controlled_buffer_7
  assign controlled_buffer_2_out = SHR ? shifter_2_out : 16'bz;  // Controlled_Buffer controlled_buffer_8
  Pull_Resistor #(.pull(1)) pull_resistor_4 (.node(pull_resistor_4_node));
  Multiplexer multiplexer_4 (.in0(1'b0), .in1(A_POSITIVE), .out(multiplexer_4_out), .sel(D_LOAD_INTO_A));  // open: en
  Multiplexer multiplexer_5 (
    .in0(multiplexer_4_out), .in1(D_LOAD_INTO_Q), .out(multiplexer_5_out), .sel(D_LOAD_INTO_Q));  // open: en
  ROM rom_2 (
    .addr(counter_2_q), .data({rom_2_data, D_LOAD_INTO_A, D_SHIFT, D_LOAD_INTO_Q, D_LOAD_INTO_M}));  // open: sel
  not not_7 (not_7_out, clock_2_out);
  Clock clock_2 (.out(clock_2_out));
  not not_8 (not_8_out, pull_resistor_4_node);
  Multiplexer #(.width(16)) multiplexer_6 (
    .in0(QDiv), .in1(Abs_Ain), .out(multiplexer_6_out), .sel(D_LOAD_INTO_Q));  // open: en
  not not_9 (not_9_out, D_LOAD_INTO_A);
  Multiplexer multiplexer_7 (.in0(Q_q0), .in1(1'b1), .out(QDiv[0]), .sel(A_POSITIVE));  // open: en
  not not_10 (not_10_out, CLK);
  assign controlled_buffer_9_out = LOAD_INTO_A ? To_Ain : 16'bz;  // Controlled_Buffer controlled_buffer_9
  Shift_Register #(.length(16)) u_A (
    .shift(SHIFT), .in(A7), .clk(MCLK), .out(A_out), .load(multiplexer_3_out), .clr(ARESET),
    .d0(controlled_buffer_9_out[15]), .q0(A7), .d1(controlled_buffer_9_out[14]), .q1(AMul[14]),
    .d2(controlled_buffer_9_out[13]), .q2(AMul[13]), .d3(controlled_buffer_9_out[12]), .q3(AMul[12]),
    .d4(controlled_buffer_9_out[11]), .q4(AMul[11]), .d5(controlled_buffer_9_out[10]), .q5(AMul[10]),
    .d6(controlled_buffer_9_out[9]), .q6(AMul[9]), .d7(controlled_buffer_9_out[8]), .q7(AMul[8]),
    .d8(controlled_buffer_9_out[7]), .q8(AMul[7]), .d9(controlled_buffer_9_out[6]), .q9(AMul[6]),
    .d10(controlled_buffer_9_out[5]), .q10(AMul[5]), .d11(controlled_buffer_9_out[4]), .q11(AMul[4]),
    .d12(controlled_buffer_9_out[3]), .q12(AMul[3]), .d13(controlled_buffer_9_out[2]), .q13(AMul[2]),
    .d14(controlled_buffer_9_out[1]), .q14(AMul[1]), .d15(controlled_buffer_9_out[0]), .q15(AMul[0]));
  or or_5 (ARESET, MRESET, RES);
  assign MCLK = not_11_out ? not_7_out : 1'bz;  // Controlled_Buffer controlled_buffer_10
  not not_11 (not_11_out, STOP);
  Counter #(.width(6), .max('h3f)) counter_4 (
    .load(not_8_out), .count(pull_resistor_4_node), .Q({counter_4_q, REPEAT}), .clk(MCLK), .clr(MRESET));  // open: D, carry
  Shift_Register #(.length(16)) Q (
    .shift(not_9_out), .in(1'b0), .clk(DCLK), .out(Q_out), .load(multiplexer_5_out),
    .d0(multiplexer_6_out[0]), .q0(Q_q0), .d1(multiplexer_6_out[1]), .q1(QDiv[1]), .d2(multiplexer_6_out[2]),
    .q2(QDiv[2]), .d3(multiplexer_6_out[3]), .q3(QDiv[3]), .d4(multiplexer_6_out[4]), .q4(QDiv[4]),
    .d5(multiplexer_6_out[5]), .q5(QDiv[5]), .d6(multiplexer_6_out[6]), .q6(QDiv[6]),
    .d7(multiplexer_6_out[7]), .q7(QDiv[7]), .d8(multiplexer_6_out[8]), .q8(QDiv[8]),
    .d9(multiplexer_6_out[9]), .q9(QDiv[9]), .d10(multiplexer_6_out[10]), .q10(QDiv[10]),
    .d11(multiplexer_6_out[11]), .q11(QDiv[11]), .d12(multiplexer_6_out[12]), .q12(QDiv[12]),
    .d13(multiplexer_6_out[13]), .q13(QDiv[13]), .d14(multiplexer_6_out[14]), .q14(QDiv[14]),
    .d15(multiplexer_6_out[15]), .q15(QDiv[15]));  // open: clr
  not not_12 (not_12_out, A[15]);
  not not_13 (not_13_out, controlled_buffer_2_out[15]);
  not not_14 (not_14_out, RESULT[15]);
  D_Flip_Flop d_ff_3 (.clk(not_10_out), .D(not_14_out), .Q(out_20), .en(MARK_FLAG), .reset(RES));  // open: Qn, preset
  assign controlled_buffer_2_out = XOR ? xor_1_out : 16'bz;  // Controlled_Buffer controlled_buffer_11
  assign xor_1_out = A ^ B;  // XOR_Gate xor_1, 16 bits wide
  and and_3 (STOP, REPEAT, counter_4_q[5]);
  not not_15 (not_15_out, B[15]);
  Multiplexer #(.select(2), .width(16)) multiplexer_8 (
    .in0(controlled_buffer_2_out), .in2({QMul, Q0}), .in3(DIV_RES), .out(RESULT), .sel({MUL_DIV_OFF, DO_DIV}));  // open: in1, en
  _16_bitni_registar u_M (
    .in_2(B), .in_1(MRESET), .Load(LOAD_INTO_M), .Clock(MCLK), .out_7(M), .OE(or_6_out));  // open: Preview
  D_Flip_Flop d_ff_4 (.clk(NMRESET), .D(A[15]), .Q(d_ff_4_q), .reset(MRESET));  // open: Qn, preset, en
  D_Flip_Flop d_ff_5 (.clk(MRESET), .D(B[15]), .Q(d_ff_5_q), .reset(NMRESET));  // open: Qn, preset, en
  assign RES_2 = GET_RES ? RESULT : 16'bz;  // Controlled_Buffer controlled_buffer_12
  Shift_Register #(.length(16)) A_2 (
    .shift(D_SHIFT), .in(Q_out), .clk(DCLK), .load(LOAD_OR_NOT), .clr(ARESET), .d0(multiplexer_9_out[0]),
    .q0(Ostatak[0]), .d1(multiplexer_9_out[1]), .q1(Ostatak[1]), .d2(multiplexer_9_out[2]), .q2(Ostatak[2]),
    .d3(multiplexer_9_out[3]), .q3(Ostatak[3]), .d4(multiplexer_9_out[4]), .q4(Ostatak[4]),
    .d5(multiplexer_9_out[5]), .q5(Ostatak[5]), .d6(multiplexer_9_out[6]), .q6(Ostatak[6]),
    .d7(multiplexer_9_out[7]), .q7(Ostatak[7]), .d8(multiplexer_9_out[8]), .q8(Ostatak[8]),
    .d9(multiplexer_9_out[9]), .q9(Ostatak[9]), .d10(multiplexer_9_out[10]), .q10(Ostatak[10]),
    .d11(multiplexer_9_out[11]), .q11(Ostatak[11]), .d12(multiplexer_9_out[12]), .q12(Ostatak[12]),
    .d13(multiplexer_9_out[13]), .q13(Ostatak[13]), .d14(multiplexer_9_out[14]), .q14(Ostatak[14]),
    .d15(multiplexer_9_out[15]), .q15(Ostatak[15]));  // open: out
  nor nor_2 (nor_2_out, RESULT[15], RESULT[14], RESULT[13], RESULT[12], RESULT[11], RESULT[10], RESULT[9], RESULT[8], RESULT[7], RESULT[6], RESULT[5], RESULT[4], RESULT[3], RESULT[2], RESULT[1], RESULT[0]);
  Shift_Register #(.length(16)) Q_2 (
    .shift(SHIFT), .in(A_out), .clk(MCLK), .load(LOAD_INTO_Q), .clr(MRESET), .d0(A[15]), .q0(QMul[15]),
    .d1(A[14]), .q1(QMul[14]), .d2(A[13]), .q2(QMul[13]), .d3(A[12]), .q3(QMul[12]), .d4(A[11]),
    .q4(QMul[11]), .d5(A[10]), .q5(QMul[10]), .d6(A[9]), .q6(QMul[9]), .d7(A[8]), .q7(QMul[8]), .d8(A[7]),
    .q8(QMul[7]), .d9(A[6]), .q9(QMul[6]), .d10(A[5]), .q10(QMul[5]), .d11(A[4]), .q11(QMul[4]), .d12(A[3]),
    .q12(QMul[3]), .d13(A[2]), .q13(QMul[2]), .d14(A[1]), .q14(QMul[1]), .d15(A[0]), .q15(Q0));  // open: out
  Multiplexer #(.width(16)) multiplexer_9 (
    .in0(Ostatak), .in1(ADivIn), .out(multiplexer_9_out), .sel(A_POSITIVE));  // open: en
  Negator #(.width(16)) negator_4 (.in(A), .out(negator_4_out));
  Negator #(.width(16)) negator_5 (.in(B), .out(negator_5_out));
  or or_6 (or_6_out, SHIFT, LOAD_INTO_A);
  and and_4 (LOAD_OR_NOT, D_LOAD_INTO_A, A_POSITIVE);
  Multiplexer #(.width(16)) multiplexer_10 (.in0(A), .in1(negator_4_out), .out(Abs_Ain), .sel(A[15]));  // open: en
  Multiplexer #(.width(16)) multiplexer_11 (.in0(B), .in1(negator_5_out), .out(Abs_Bin), .sel(B[15]));  // open: en
  and and_5 (and_5_out, not_15_out, not_12_out, controlled_buffer_2_out[15]);
  and and_6 (and_6_out, B[15], A[15], not_13_out);
  or or_7 (or_7_out, and_5_out, and_6_out);
  xor xor_2 (xor_2_out, d_ff_4_q, d_ff_5_q);
  xor xor_3 (xor_3_out, d_ff_4_q, Ostatak[15]);
  and and_7 (and_7_out, MARK_FLAG, nor_2_out, GET_RES);
  not not_16 (not_16_out, CLK);
  D_Flip_Flop KomplementRezultata (
    .clk(DSTOP), .D(xor_2_out), .Q(KOMPLEMENT_REZULTATA), .reset(MRESET));  // open: Qn, preset, en
  D_Flip_Flop d_ff_6 (.clk(not_16_out), .D(and_7_out), .Q(ZERO), .en(MARK_FLAG), .reset(RES));  // open: Qn, preset
  _16_bitni_registar u_16_bitni_registar_1 (
    .in_2(Abs_Bin), .in_1(MRESET), .Load(D_LOAD_INTO_M), .Clock(DCLK), .Preview(MDiv));  // open: out_7, OE
  D_Flip_Flop KomplementOstatka (
    .clk(DSTOP), .D(xor_3_out), .Q(KOMPLEMENT_OSTATKA), .reset(MRESET));  // open: Qn, preset, en
  not not_17 (not_17_out, CLK);
  or or_8 (or_8_out, STOP, DSTOP);
  D_Flip_Flop d_ff_7 (.clk(not_17_out), .D(or_7_out), .Q(OVERFLOW), .en(MARK_FLAG), .reset(RES));  // open: Qn, preset
  or or_9 (FINISHED, STOP, DSTOP);
  D_Flip_Flop Q_1 (.clk(MCLK), .D(Q0), .Q(Q_1_q), .reset(MRESET));  // open: Qn, preset, en
  Adder #(.width(16)) adder_2 (.a({A7, AMul}), .b(M), .out(adder_2_out));  // open: cin, cout
  Subtractor #(.width(16)) subtractor_3 (.a({A7, AMul}), .b(M), .out(subtractor_3_out));  // open: bin, bout
  not not_18 (not_18_out, Q_1_q);
  not not_19 (not_19_out, Q0);
  Multiplexer #(.width(16)) multiplexer_12 (.in0({A7, AMul}), .in1(DIV_REM), .out(High), .sel(d_ff_8_q));  // open: en
  D_Flip_Flop d_ff_8 (.clk(or_8_out), .D(DO_DIV), .Q(d_ff_8_q));  // open: Qn, preset, en, reset
  Multiplexer #(.select(2), .width(16)) multiplexer_13 (
    .in0({A7, AMul}), .in1(adder_2_out), .in2(subtractor_3_out), .out(To_Ain), .sel({A_M_t, A_M}));  // open: in3, en
  and and_8 (A_M, Q_1_q, not_19_out);
  and and_9 (A_M_t, not_18_out, Q0);

  // Other names for the same wires on the sheet: Ain[15:0] = A; AMul[15] = A7; Bin[15:0] = B; QMul[0] = Q0;
  //   RESET = RES; SHIFT_AMOUNT[3:0] = B[3:0]

  // Notes on the sheet:
  //   contents of rom_1 (hex, n*v repeats v):
  //   3 4 8 4 8 4 8 4 8 4 8 4 8 4 8 4 8 4 8 4 8 4 8 4 8 4 8 4 8 4 8 4 8 10
  //   contents of rom_2 (hex, n*v repeats v):
  //   3 4 8 4 8 4 8 4 8 4 8 4 8 4 8 4 8 4 8 4 8 4 8 4 8 4 8 4 8 4 8 4 8 10
  //   SR
  //   SA
  //   SA'
  //   SR'
  //   SB
  //   SB'
  //   POSITIVE
endmodule

module VideoMemorija (
  input  [15:0] data_bus,
  input  [1:0] select_mask,
  input  [15:0] address_bus,
  input  MEM_WR,
  input  RESET,
  output [31:0] P7,
  output [31:0] P6,
  output [31:0] P5,
  output [31:0] P4,
  output [31:0] P3,
  output [31:0] P2,
  output [31:0] P1,
  output [31:0] P0
);

  wire and_1_out, CLK, comparator_1_eq, D1, D2, D3, D4, D5, D6, D7, decoder_1_out0, demultiplexer_2_out0,
       demultiplexer_2_out1, demultiplexer_2_out2, demultiplexer_2_out3, demultiplexer_5_out0,
       demultiplexer_5_out1, demultiplexer_5_out2, demultiplexer_5_out3, demultiplexer_7_out0,
       demultiplexer_7_out1, demultiplexer_7_out2, demultiplexer_7_out3, demultiplexer_9_out0,
       demultiplexer_9_out1, demultiplexer_9_out2, demultiplexer_9_out3, demultiplexer_11_out0,
       demultiplexer_11_out1, demultiplexer_11_out2, demultiplexer_11_out3, demultiplexer_13_out0,
       demultiplexer_13_out1, demultiplexer_13_out2, demultiplexer_13_out3, demultiplexer_15_out0,
       demultiplexer_15_out1, demultiplexer_15_out2, demultiplexer_15_out3, demultiplexer_17_out0,
       demultiplexer_17_out1, demultiplexer_17_out2, demultiplexer_17_out3, demultiplexer_19_out0,
       demultiplexer_19_out1, demultiplexer_19_out2, demultiplexer_19_out3, SELECT;
  wire [1:0] CHAR;
  wire [2:0] counter_3_q;
  wire [3:0] counter_2_q;
  wire [7:0] demultiplexer_3_out0, demultiplexer_4_out0, demultiplexer_4_out1, demultiplexer_4_out2,
       demultiplexer_4_out3, demultiplexer_6_out0, demultiplexer_6_out1, demultiplexer_6_out2,
       demultiplexer_6_out3, demultiplexer_8_out0, demultiplexer_8_out1, demultiplexer_8_out2,
       demultiplexer_8_out3, demultiplexer_10_out0, demultiplexer_10_out1, demultiplexer_10_out2,
       demultiplexer_10_out3, demultiplexer_12_out0, demultiplexer_12_out1, demultiplexer_12_out2,
       demultiplexer_12_out3, demultiplexer_14_out0, demultiplexer_14_out1, demultiplexer_14_out2,
       demultiplexer_14_out3, demultiplexer_16_out0, demultiplexer_16_out1, demultiplexer_16_out2,
       demultiplexer_16_out3, demultiplexer_18_out0, demultiplexer_18_out1, demultiplexer_18_out2,
       demultiplexer_18_out3, L1, L2, L3, L4, L5, L6, L7, rom_1_data;
  wire [15:0] adder_1_out, demultiplexer_1_out0, demultiplexer_1_out1, demultiplexer_1_out2,
       demultiplexer_1_out3, multiplexer_1_out, register_1_q, register_2_q, register_3_q, register_4_q,
       shifter_1_out;

  Demultiplexer #(.select(2), .width(16)) demultiplexer_1 (
    .out0(demultiplexer_1_out0), .out1(demultiplexer_1_out1), .out2(demultiplexer_1_out2),
    .out3(demultiplexer_1_out3), .in(data_bus), .sel(address_bus[1:0]), .en(SELECT));
  Demultiplexer #(.select(2)) demultiplexer_2 (
    .out0(demultiplexer_2_out0), .out1(demultiplexer_2_out1), .out2(demultiplexer_2_out2),
    .out3(demultiplexer_2_out3), .in(SELECT), .sel(address_bus[1:0]));  // open: en
  Comparator #(.width(2)) comparator_1 (.a(select_mask), .b(address_bus[3:2]), .eq(comparator_1_eq));  // open: gt, lt
  and and_1 (and_1_out, address_bus[12], address_bus[13], address_bus[14], address_bus[15]);
  and and_2 (SELECT, comparator_1_eq, and_1_out, MEM_WR);
  Register #(.width(16)) register_1 (
    .D(demultiplexer_1_out3), .en(demultiplexer_2_out3), .Q(register_1_q), .clk(CLK), .clr(RESET));
  Register #(.width(16)) register_2 (
    .D(demultiplexer_1_out2), .en(demultiplexer_2_out2), .Q(register_2_q), .clk(CLK), .clr(RESET));
  Register #(.width(16)) register_3 (
    .D(demultiplexer_1_out1), .en(demultiplexer_2_out1), .Q(register_3_q), .clk(CLK), .clr(RESET));
  Register #(.width(16)) register_4 (
    .D(demultiplexer_1_out0), .en(demultiplexer_2_out0), .Q(register_4_q), .clk(CLK), .clr(RESET));
  Multiplexer #(.select(2), .width(16)) multiplexer_1 (
    .in0(register_1_q), .in1(register_2_q), .in2(register_3_q), .in3(register_4_q), .out(multiplexer_1_out),
    .sel(CHAR));  // open: en
  Counter #(.width(2), .max('h3)) counter_1 (.Q(CHAR), .clk(CLK), .clr(RESET));  // open: load, D, count, carry
  Shifter #(.width(16)) shifter_1 (.in({{8{1'b0}}, multiplexer_1_out[7:0]}), .\dist (4'b0011), .out(shifter_1_out));
  Clock clock_1 (.out(CLK));
  Adder #(.width(16)) adder_1 (.a(shifter_1_out), .b({{13{1'b0}}, counter_3_q}), .out(adder_1_out));  // open: cin, cout
  Counter #(.width(4), .max('hf)) counter_2 (.Q(counter_2_q), .clk(CLK), .clr(RESET));  // open: load, D, count, carry
  DotMatrix #(.inputtype("row"), .matrixcols(32), .matrixrows(8)) dotmatrix_1 (
    .row0(P0), .row1(P1), .row2(P2), .row3(P3), .row4(P4), .row5(P5), .row6(P6), .row7(P7));
  Counter #(.width(3), .max('h7)) counter_3 (
    .Q(counter_3_q), .clk(counter_2_q[1]), .clr(RESET));  // open: load, D, count, carry
  Decoder #(.select(3)) decoder_1 (
    .out0(decoder_1_out0), .out1(D1), .out2(D2), .out3(D3), .out4(D4), .out5(D5), .out6(D6), .out7(D7),
    .sel(counter_3_q));  // open: en
  Demultiplexer #(.select(3), .width(8)) demultiplexer_3 (
    .out0(demultiplexer_3_out0), .out1(L1), .out2(L2), .out3(L3), .out4(L4), .out5(L5), .out6(L6), .out7(L7),
    .in(rom_1_data), .sel(counter_3_q));  // open: en
  ROM #(.addrWidth(16)) rom_1 (.addr(adder_1_out), .data(rom_1_data));  // open: sel
  Demultiplexer #(.select(2), .width(8)) demultiplexer_4 (
    .out0(demultiplexer_4_out0), .out1(demultiplexer_4_out1), .out2(demultiplexer_4_out2),
    .out3(demultiplexer_4_out3), .in(demultiplexer_3_out0), .sel(CHAR));  // open: en
  Demultiplexer #(.select(2)) demultiplexer_5 (
    .out0(demultiplexer_5_out0), .out1(demultiplexer_5_out1), .out2(demultiplexer_5_out2),
    .out3(demultiplexer_5_out3), .in(decoder_1_out0), .sel(CHAR));  // open: en
  Demultiplexer #(.select(2), .width(8)) demultiplexer_6 (
    .out0(demultiplexer_6_out0), .out1(demultiplexer_6_out1), .out2(demultiplexer_6_out2),
    .out3(demultiplexer_6_out3), .in(L4), .sel(CHAR));  // open: en
  Demultiplexer #(.select(2)) demultiplexer_7 (
    .out0(demultiplexer_7_out0), .out1(demultiplexer_7_out1), .out2(demultiplexer_7_out2),
    .out3(demultiplexer_7_out3), .in(D4), .sel(CHAR));  // open: en
  Register register_5 (.D(demultiplexer_4_out0), .en(demultiplexer_5_out0), .Q(P0[7:0]), .clk(CLK), .clr(RESET));
  Register register_6 (.D(demultiplexer_4_out1), .en(demultiplexer_5_out1), .Q(P0[15:8]), .clk(CLK), .clr(RESET));
  Register register_7 (.D(demultiplexer_4_out2), .en(demultiplexer_5_out2), .Q(P0[23:16]), .clk(CLK), .clr(RESET));
  Register register_8 (.D(demultiplexer_4_out3), .en(demultiplexer_5_out3), .Q(P0[31:24]), .clk(CLK), .clr(RESET));
  Register register_9 (.D(demultiplexer_6_out0), .en(demultiplexer_7_out0), .Q(P4[7:0]), .clk(CLK), .clr(RESET));
  Register register_10 (.D(demultiplexer_6_out1), .en(demultiplexer_7_out1), .Q(P4[15:8]), .clk(CLK), .clr(RESET));
  Register register_11 (.D(demultiplexer_6_out2), .en(demultiplexer_7_out2), .Q(P4[23:16]), .clk(CLK), .clr(RESET));
  Register register_12 (.D(demultiplexer_6_out3), .en(demultiplexer_7_out3), .Q(P4[31:24]), .clk(CLK), .clr(RESET));
  Demultiplexer #(.select(2), .width(8)) demultiplexer_8 (
    .out0(demultiplexer_8_out0), .out1(demultiplexer_8_out1), .out2(demultiplexer_8_out2),
    .out3(demultiplexer_8_out3), .in(L1), .sel(CHAR));  // open: en
  Demultiplexer #(.select(2)) demultiplexer_9 (
    .out0(demultiplexer_9_out0), .out1(demultiplexer_9_out1), .out2(demultiplexer_9_out2),
    .out3(demultiplexer_9_out3), .in(D1), .sel(CHAR));  // open: en
  Demultiplexer #(.select(2), .width(8)) demultiplexer_10 (
    .out0(demultiplexer_10_out0), .out1(demultiplexer_10_out1), .out2(demultiplexer_10_out2),
    .out3(demultiplexer_10_out3), .in(L5), .sel(CHAR));  // open: en
  Demultiplexer #(.select(2)) demultiplexer_11 (
    .out0(demultiplexer_11_out0), .out1(demultiplexer_11_out1), .out2(demultiplexer_11_out2),
    .out3(demultiplexer_11_out3), .in(D5), .sel(CHAR));  // open: en
  Register register_13 (.D(demultiplexer_8_out0), .en(demultiplexer_9_out0), .Q(P1[7:0]), .clk(CLK), .clr(RESET));
  Register register_14 (.D(demultiplexer_8_out1), .en(demultiplexer_9_out1), .Q(P1[15:8]), .clk(CLK), .clr(RESET));
  Register register_15 (.D(demultiplexer_8_out2), .en(demultiplexer_9_out2), .Q(P1[23:16]), .clk(CLK), .clr(RESET));
  Register register_16 (.D(demultiplexer_8_out3), .en(demultiplexer_9_out3), .Q(P1[31:24]), .clk(CLK), .clr(RESET));
  Register register_17 (.D(demultiplexer_10_out0), .en(demultiplexer_11_out0), .Q(P5[7:0]), .clk(CLK), .clr(RESET));
  Register register_18 (.D(demultiplexer_10_out1), .en(demultiplexer_11_out1), .Q(P5[15:8]), .clk(CLK), .clr(RESET));
  Register register_19 (.D(demultiplexer_10_out2), .en(demultiplexer_11_out2), .Q(P5[23:16]), .clk(CLK), .clr(RESET));
  Register register_20 (.D(demultiplexer_10_out3), .en(demultiplexer_11_out3), .Q(P5[31:24]), .clk(CLK), .clr(RESET));
  Demultiplexer #(.select(2), .width(8)) demultiplexer_12 (
    .out0(demultiplexer_12_out0), .out1(demultiplexer_12_out1), .out2(demultiplexer_12_out2),
    .out3(demultiplexer_12_out3), .in(L2), .sel(CHAR));  // open: en
  Demultiplexer #(.select(2)) demultiplexer_13 (
    .out0(demultiplexer_13_out0), .out1(demultiplexer_13_out1), .out2(demultiplexer_13_out2),
    .out3(demultiplexer_13_out3), .in(D2), .sel(CHAR));  // open: en
  Demultiplexer #(.select(2), .width(8)) demultiplexer_14 (
    .out0(demultiplexer_14_out0), .out1(demultiplexer_14_out1), .out2(demultiplexer_14_out2),
    .out3(demultiplexer_14_out3), .in(L6), .sel(CHAR));  // open: en
  Demultiplexer #(.select(2)) demultiplexer_15 (
    .out0(demultiplexer_15_out0), .out1(demultiplexer_15_out1), .out2(demultiplexer_15_out2),
    .out3(demultiplexer_15_out3), .in(D6), .sel(CHAR));  // open: en
  Register register_21 (.D(demultiplexer_12_out0), .en(demultiplexer_13_out0), .Q(P2[7:0]), .clk(CLK), .clr(RESET));
  Register register_22 (.D(demultiplexer_12_out1), .en(demultiplexer_13_out1), .Q(P2[15:8]), .clk(CLK), .clr(RESET));
  Register register_23 (.D(demultiplexer_12_out2), .en(demultiplexer_13_out2), .Q(P2[23:16]), .clk(CLK), .clr(RESET));
  Register register_24 (.D(demultiplexer_12_out3), .en(demultiplexer_13_out3), .Q(P2[31:24]), .clk(CLK), .clr(RESET));
  Register register_25 (.D(demultiplexer_14_out0), .en(demultiplexer_15_out0), .Q(P6[7:0]), .clk(CLK), .clr(RESET));
  Register register_26 (.D(demultiplexer_14_out1), .en(demultiplexer_15_out1), .Q(P6[15:8]), .clk(CLK), .clr(RESET));
  Register register_27 (.D(demultiplexer_14_out2), .en(demultiplexer_15_out2), .Q(P6[23:16]), .clk(CLK), .clr(RESET));
  Register register_28 (.D(demultiplexer_14_out3), .en(demultiplexer_15_out3), .Q(P6[31:24]), .clk(CLK), .clr(RESET));
  Demultiplexer #(.select(2), .width(8)) demultiplexer_16 (
    .out0(demultiplexer_16_out0), .out1(demultiplexer_16_out1), .out2(demultiplexer_16_out2),
    .out3(demultiplexer_16_out3), .in(L3), .sel(CHAR));  // open: en
  Demultiplexer #(.select(2)) demultiplexer_17 (
    .out0(demultiplexer_17_out0), .out1(demultiplexer_17_out1), .out2(demultiplexer_17_out2),
    .out3(demultiplexer_17_out3), .in(D3), .sel(CHAR));  // open: en
  Demultiplexer #(.select(2), .width(8)) demultiplexer_18 (
    .out0(demultiplexer_18_out0), .out1(demultiplexer_18_out1), .out2(demultiplexer_18_out2),
    .out3(demultiplexer_18_out3), .in(L7), .sel(CHAR));  // open: en
  Demultiplexer #(.select(2)) demultiplexer_19 (
    .out0(demultiplexer_19_out0), .out1(demultiplexer_19_out1), .out2(demultiplexer_19_out2),
    .out3(demultiplexer_19_out3), .in(D7), .sel(CHAR));  // open: en
  Register register_29 (.D(demultiplexer_16_out0), .en(demultiplexer_17_out0), .Q(P3[7:0]), .clk(CLK), .clr(RESET));
  Register register_30 (.D(demultiplexer_16_out1), .en(demultiplexer_17_out1), .Q(P3[15:8]), .clk(CLK), .clr(RESET));
  Register register_31 (.D(demultiplexer_16_out2), .en(demultiplexer_17_out2), .Q(P3[23:16]), .clk(CLK), .clr(RESET));
  Register register_32 (.D(demultiplexer_16_out3), .en(demultiplexer_17_out3), .Q(P3[31:24]), .clk(CLK), .clr(RESET));
  Register register_33 (.D(demultiplexer_18_out0), .en(demultiplexer_19_out0), .Q(P7[7:0]), .clk(CLK), .clr(RESET));
  Register register_34 (.D(demultiplexer_18_out1), .en(demultiplexer_19_out1), .Q(P7[15:8]), .clk(CLK), .clr(RESET));
  Register register_35 (.D(demultiplexer_18_out2), .en(demultiplexer_19_out2), .Q(P7[23:16]), .clk(CLK), .clr(RESET));
  Register register_36 (.D(demultiplexer_18_out3), .en(demultiplexer_19_out3), .Q(P7[31:24]), .clk(CLK), .clr(RESET));

  // Notes on the sheet:
  //   contents of rom_1 (hex, n*v repeats v):
  //   384*0 1c 26 4*2a 32 1c 1 3 5 9 4*1 c 12 2 4 8 10 10 1e c 12 2 4 2 2 12 c 2 6 a 12 1e 2 2 2 1e 10 10
  //   c 2 2 12 c c 12 10 10 1e 12 12 c 1e 2 2 2 4*4 c 12 12 c 12 12 12 c c 12 12 e 2 2 12 c 56*0 c 12 12
  //   12 1e 12 12 12 1c 12 12 1c 12 12 12 1c c 12 4*10 12 c 1c 6*12 1c 1e 10 10 1c 10 10 10 1e 1e 10 1c
  //   5*10 c 12 10 1e 12 12 12 c 12 12 12 1e 4*12 8*4 6*2 12 c 12 12 14 18 14 12 12 12 7*10 1e 22 36 2a
  //   6*22 32 2a 2a 26 26 26 22 c 6*12 c 1c 12 12 1c 4*10 c 4*12 16 16 e 1c 12 12 1c 14 12 12 12 c 12 10 c
  //   2 2 12 c 3e 7*8 7*12 c 6*22 14 8 5*22 2a 2a 14 22 22 14 8 14 14 2 22 22 22 14 5*8 1e 2 4 8 10 10 10
  //   1e
endmodule

module _8_bitna_displej_logika (
  input  [15:0] ULAZ,
  output [3:0] out_2,
  output [3:0] out_3,
  output [3:0] out_4,
  output [3:0] out_5
);

  Hex_Digit_Display hex_digit_display_1 (.value(ULAZ[15:12]));  // open: dp
  Hex_Digit_Display hex_digit_display_2 (.value(ULAZ[11:8]));  // open: dp
  Hex_Digit_Display hex_digit_display_3 (.value(ULAZ[7:4]));  // open: dp
  Hex_Digit_Display hex_digit_display_4 (.value(ULAZ[3:0]));  // open: dp

  assign out_2 = ULAZ[7:4];
  assign out_3 = ULAZ[3:0];
  assign out_4 = ULAZ[15:12];
  assign out_5 = ULAZ[11:8];

  // Other names for the same wires on the sheet: prvih_4_bita[3:0] = ULAZ[3:0]; drugih_4_bita[3:0] = ULAZ[7:4];
  //   trećih_4_bita[3:0] = ULAZ[11:8]; četvrtih_4_bita[3:0] = ULAZ[15:12]
endmodule

module _9_bitna_displej_logika (
  input  [8:0] in_1,
  output [3:0] out_2,
  output [3:0] out_3,
  output [3:0] out_4
);

  Hex_Digit_Display hex_digit_display_1 (.value({3'b000, in_1[8]}));  // open: dp
  Hex_Digit_Display hex_digit_display_2 (.value(in_1[7:4]));  // open: dp
  Hex_Digit_Display hex_digit_display_3 (.value(in_1[3:0]));  // open: dp

  assign out_2 = {3'b000, in_1[8]};
  assign out_3 = in_1[7:4];
  assign out_4 = in_1[3:0];
endmodule
